# Fritzing sketch Acender e Apagar LED (saved by Fritzing 0.9.0b)
breadboards: 1

parts:
  Componente1 = Arduino Uno (Rev3)
  S1 = Pushbutton [package="[THT]"]
  S2 = Pushbutton [package="[THT]"]
  LED1 = LED - 5mm [color="Red (633nm)" package="5 mm [THT]"]
  R1 = Resistor [tolerance=±5% resistance=10k package="0805 [SMD]"]
  R2 = Resistor [tolerance=±20% resistance=10k package="0805 [SMD]"]
  R4 = Resistor [tolerance=±1% resistance=300 package="0805 [SMD]"]

nets:
  N1: Componente1.D8, S1.Pin_1, S1.Pin_2, R1.Pin_0
  N2: Componente1.D9_PWM, S2.Pin_1, S2.Pin_2, R2.Pin_0
  N3: Componente1.D10_PWM/SS, R4.Pin_0
  N4: Componente1.5V, S1.Pin_3, S1.Pin_4, S2.Pin_3, S2.Pin_4
  N5: Componente1.GND, LED1.cathode, R1.Pin_1, R2.Pin_1
  N6: LED1.anode, R4.Pin_1
