# Fritzing sketch Potênciometro (saved by Fritzing 0.9.0b)
breadboards: 1

parts:
  Componente1 = Arduino Uno (Rev3)
  LED1 = LEDs [package=led10mm]
  R1_300k = Resistor [package="2010 [SMD]"]
  R3 = Rotary Potentiometer (Large) [maximum_resistance=100kΩ package=THT]

nets:
  N1: Componente1.A0, R3.wiper
  N2: Componente1.D6_PWM, R1_300k.Pin_1
  N3: Componente1.5V, R3.leg2
  N4: Componente1.GND, LED1.A, R3.leg1
  N5: LED1.C, R1_300k.Pin_0
