# Fritzing sketch Sensor de Luminosidade (saved by Fritzing 0.9.0b)
breadboards: 1

parts:
  Componente1 = Arduino Uno (Rev3)
  LED1 = LEDs [package=led10mm]
  R1_300k = Resistor [package="2010 [SMD]"]
  R1_10k = Resistor [tolerance=±5% resistance=10k package=THT]
  R1 = Photocell (LDR) [package=THT]

nets:
  N1: Componente1.A0, R1_10k.Pin_1, R1.pin_0
  N2: Componente1.D6_PWM, R1_300k.Pin_1
  N3: Componente1.5V, R1.pin_1
  N4: Componente1.GND, LED1.A, R1_10k.Pin_0
  N5: LED1.C, R1_300k.Pin_0
