# Fritzing sketch Sistema de Monitoramento (saved by Fritzing 0.9.2b)
breadboards: 1

parts:
  R1 = Resistor [tolerance=±5% resistance=10k package=THT]
  R2 = Resistor [tolerance=±5% resistance=10k package=THT]
  R3 = Resistor [tolerance=±5% resistance=10k package=THT]
  S1 = Pushbutton [package="[THT]"]
  R4 = Photocell (LDR) [package=THT]
  R5 = Rotary Potentiometer (Large) [maximum_resistance=100kΩ package=THT]
  R6 = Temperature Sensor (Thermistor) [thermistor_type=NTC package=THT]
  Componente1 = Arduino Uno (Rev3) - ICSP
  LCD1 = LCD screen

nets:
  5V: R1.Pin_0, R2.Pin_1, R3.Pin_0, R5.leg1, Componente1.5V, LCD1.VDD
  N1: R1.Pin_1, R4.pin_0, Componente1.A0
  N2: R2.Pin_0, S1.Pin_1, S1.Pin_2, Componente1.D2
  N3: R3.Pin_1, R6.pin_0, Componente1.A1
  GND: S1.Pin_3, S1.Pin_4, R4.pin_1, R5.leg2, R6.pin_1, Componente1.GND, LCD1.VSS, LCD1.R/W
  N4: R5.wiper, LCD1.V0
  N5: Componente1.ICSP_MISO, Componente1.D12/MISO, LCD1.RS
  N6: Componente1.ICSP_MOSI, Componente1.D11_PWM/MOSI, LCD1.E
  N7: Componente1.D4, LCD1.DB7
  N8: Componente1.D5_PWM, LCD1.DB6
  N9: Componente1.D6_PWM, LCD1.DB5
  N10: Componente1.D7, LCD1.DB4
