# Fritzing sketch Sensor de Monitoramento (saved by Fritzing 0.9.0b)
breadboards: 1

parts:
  Componente1 = SRF05 Ultrasonic Rangefinder
  Componente2 = Arduino Uno (Rev3) - ICSP
  J1 = Piezo Speaker
  R1 = Resistor [tolerance=±5% resistance=300 package=THT]
  LED1 = LED - 3mm [color="Red (633nm)" package="3 mm [THT]"]
  LED2 = LED - 3mm [color="Yellow (585nm)" package="3 mm [THT]"]
  LED3 = LED - 3mm [color="Green (555nm)" package="3 mm [THT]"]
  R2 = Resistor [tolerance=±5% resistance=300 package=THT]
  R3 = Resistor [tolerance=±5% resistance=300 package=THT]
  R4 = Resistor [tolerance=±5% resistance=300 package=THT]

nets:
  VCC: Componente1.VCC, Componente2.5V
  N1: Componente1.Trig, Componente2.ICSP_MISO, Componente2.D12/MISO
  N2: Componente1.Echo, Componente2.D13/SCK
  GND: Componente1.GND, Componente2.GND, J1.pin1, LED1.cathode, LED2.cathode, LED3.cathode
  N3: Componente2.ICSP_MOSI, Componente2.D11_PWM/MOSI, R1.Pin_1
  N4: Componente2.D8, R3.Pin_1
  N5: Componente2.D9_PWM, R2.Pin_1
  N6: Componente2.D7, R4.Pin_1
  N7: J1.pin2, R1.Pin_0
  N8: LED1.anode, R2.Pin_0
  N9: LED2.anode, R3.Pin_0
  N10: LED3.anode, R4.Pin_0
