# Fritzing sketch Semáforo (saved by Fritzing 0.9.0b)
breadboards: 1

parts:
  S2 = Pushbutton [package="[THT]"]
  S3 = Pushbutton [package="[THT]"]
  R2_10k = Resistor [tolerance=±5% resistance=10k package=THT]
  R1_10k = Resistor [tolerance=±5% resistance=10k package=THT]
  Componente1 = Arduino Uno (Rev3)
  LED1_vermelho1 = LED - 5mm [color="Red (633nm)" package="5 mm [THT]"]
  LED1_verde2 = LED - 5mm [color="Green (555nm)" package="5 mm [THT]"]
  LED2_verde1 = LED - 5mm [color="Green (555nm)" package="5 mm [THT]"]
  LED1_amarelo1 = LED - 5mm [color="Yellow (585nm)" package="5 mm [THT]"]
  LED2_vermelho1 = LED - 5mm [color="Red (633nm)" package="5 mm [THT]"]
  LED2_amarelo1 = LED - 5mm [color="Yellow (585nm)" package="5 mm [THT]"]
  R6_300_ohm1 = Resistor [tolerance=±5% resistance=300 package=THT]
  R5_300_ohm1 = Resistor [tolerance=±5% resistance=300 package=THT]
  R4_300_ohm1 = Resistor [tolerance=±5% resistance=300 package=THT]
  R3_300_ohm1 = Resistor [tolerance=±5% resistance=300 package=THT]
  R1_300_ohm1 = Resistor [tolerance=±5% resistance=300 package=THT]
  R2_300_ohm1 = Resistor [tolerance=±5% resistance=300 package=THT]

nets:
  N1: S2.Pin_1, S2.Pin_2, R2_10k.Pin_1, Componente1.D1/TX
  N2: S2.Pin_3, S2.Pin_4, S3.Pin_3, S3.Pin_4, Componente1.GND, LED1_vermelho1.cathode, LED1_verde2.cathode, LED2_verde1.cathode, LED1_amarelo1.cathode, LED2_vermelho1.cathode, LED2_amarelo1.cathode
  N3: S3.Pin_1, S3.Pin_2, R1_10k.Pin_1, Componente1.D0/RX
  N4: R2_10k.Pin_0, R1_10k.Pin_0, Componente1.5V
  N5: Componente1.D8, R2_300_ohm1.Pin_1
  N6: Componente1.D9_PWM, R1_300_ohm1.Pin_1
  N7: Componente1.D4, R6_300_ohm1.Pin_1
  N8: Componente1.D5_PWM, R5_300_ohm1.Pin_1
  N9: Componente1.D6_PWM, R4_300_ohm1.Pin_1
  N10: Componente1.D7, R3_300_ohm1.Pin_1
  N11: LED1_vermelho1.anode, R1_300_ohm1.Pin_0
  N12: LED1_verde2.anode, R3_300_ohm1.Pin_0
  N13: LED2_verde1.anode, R6_300_ohm1.Pin_0
  N14: LED1_amarelo1.anode, R2_300_ohm1.Pin_0
  N15: LED2_vermelho1.anode, R4_300_ohm1.Pin_0
  N16: LED2_amarelo1.anode, R5_300_ohm1.Pin_0
