# Fritzing sketch ArvoreNatal (saved by Fritzing 0.9.2b)
breadboards: 1

parts:
  Componente1 = Arduino Uno (Rev3)
  LED1 = LED - 5mm [color="Red (633nm)" package="5 mm [THT]"]  # not connected
  LED2 = LED - 5mm [color="Red (633nm)" package="5 mm [THT]"]  # not connected
  LED3 = LED - 5mm [color="Red (633nm)" package="5 mm [THT]"]  # not connected
  LED4 = LED - 5mm [color="Red (633nm)" package="5 mm [THT]"]  # not connected
  LED5 = LED - 5mm [color="Red (633nm)" package="5 mm [THT]"]  # not connected
  LED6 = LED - 5mm [color="Red (633nm)" package="5 mm [THT]"]  # not connected
  R1 = Resistor [tolerance=±5% resistance=220 package=THT]
  R2 = Resistor [tolerance=±5% resistance=220 package=THT]
  R3 = Resistor [tolerance=±5% resistance=220 package=THT]
  R4 = Resistor [tolerance=±5% resistance=220 package=THT]
  R5 = Resistor [tolerance=±5% resistance=220 package=THT]
  R6 = Resistor [tolerance=±5% resistance=220 package=THT]
  R7 = Resistor [tolerance=±5% resistance=220 package=THT]
  S1 = Pushbutton [package="[THT]"]

nets:
  N1: Componente1.D8, R7.Pin_0, S1.Pin_1, S1.Pin_2
  N2: Componente1.D2, R1.Pin_0
  N3: Componente1.D3_PWM, R2.Pin_0
  N4: Componente1.D4, R3.Pin_0
  N5: Componente1.D5_PWM, R4.Pin_0
  N6: Componente1.D6_PWM, R5.Pin_1
  N7: Componente1.D7, R6.Pin_0
  N8: Componente1.5V, S1.Pin_3, S1.Pin_4
  N9: Componente1.GND, R7.Pin_1
