# Fritzing sketch Alarme Ultrassonico (saved by Fritzing 0.9.2b)
breadboards: 1

parts:
  Componente1 = Arduino Uno (Rev3)
  S1 = Pushbutton [package="[THT]"]
  J1 = Piezo Speaker
  R1 = Resistor [tolerance=±5% resistance=220 package=THT]
  LED1 = LED - 5mm [color="Red (633nm)" package="5 mm [THT]"]
  LED2 = LED - 5mm [color="Green (570nm)" package="5 mm [THT]"]
  R2 = Resistor [tolerance=±5% resistance=220 package=THT]
  R3 = Resistor [tolerance=±5% resistance=220 package=THT]
  Componente2 = SRF05 Ultrasonic Rangefinder

nets:
  N1: Componente1.D8, S1.Pin_3, S1.Pin_4, R1.Pin_0
  N2: Componente1.D3_PWM, J1.pin2
  N3: Componente1.D4, Componente2.Echo
  N4: Componente1.D5_PWM, Componente2.Trig
  N5: Componente1.D6_PWM, R2.Pin_1
  N6: Componente1.D7, R3.Pin_1
  5V: Componente1.5V, S1.Pin_1, S1.Pin_2, Componente2.VCC
  GND: Componente1.GND, J1.pin1, R1.Pin_1, LED1.cathode, LED2.cathode, Componente2.GND
  N7: LED1.anode, R3.Pin_0
  N8: LED2.anode, R2.Pin_0
