# Fritzing sketch Esquematico (saved by Fritzing 0.9.2b)
breadboards: 1

parts:
  Componente1 = Arduino Uno (Rev3)
  S1 = Pushbutton [package="[THT]"]
  S2 = Pushbutton [package="[THT]"]
  S3 = Pushbutton [package="[THT]"]
  S4 = Pushbutton [package="[THT]"]
  S5 = Pushbutton [package="[THT]"]
  S6 = Pushbutton [package="[THT]"]
  S7 = Pushbutton [package="[THT]"]
  J1 = Piezo Speaker
  R1 = Resistor [tolerance=±5% resistance=220 package=THT]
  R2 = Resistor [tolerance=±5% resistance=220 package=THT]
  R3 = Resistor [tolerance=±5% resistance=220 package=THT]
  R4 = Resistor [tolerance=±5% resistance=220 package=THT]
  R5 = Resistor [tolerance=±5% resistance=220 package=THT]
  R6 = Resistor [tolerance=±5% resistance=220 package=THT]
  R7 = Resistor [tolerance=±5% resistance=220 package=THT]

nets:
  N1: Componente1.D8, S7.Pin_1, S7.Pin_2, R1.Pin_1
  N2: Componente1.D12/MISO, J1.pin2
  N3: Componente1.D2, S1.Pin_1, S1.Pin_2, R7.Pin_1
  N4: Componente1.D3_PWM, S2.Pin_1, S2.Pin_2, R6.Pin_1
  N5: Componente1.D4, S3.Pin_1, S3.Pin_2, R5.Pin_1
  N6: Componente1.D5_PWM, S4.Pin_1, S4.Pin_2, R4.Pin_1
  N7: Componente1.D6_PWM, S5.Pin_1, S5.Pin_2, R3.Pin_1
  N8: Componente1.D7, S6.Pin_1, S6.Pin_2, R2.Pin_1
  N9: Componente1.5V, S1.Pin_3, S1.Pin_4, S2.Pin_3, S2.Pin_4, S3.Pin_3, S3.Pin_4, S4.Pin_3, S4.Pin_4, S5.Pin_3, S5.Pin_4, S6.Pin_3, S6.Pin_4, S7.Pin_3, S7.Pin_4
  N10: Componente1.GND, J1.pin1, R1.Pin_0, R3.Pin_0, R4.Pin_0, R5.Pin_0, R6.Pin_0, R7.Pin_0
