# Fritzing sketch Sensor de Umidade e Temperatura (saved by Fritzing 0.9.2b)
breadboards: 1

parts:
  Componente1 = Arduino Uno (Rev3)
  LCD1 = LCD screen
  U1 = POT [package=pot_alpha_rv16af-20]
  RHT1 = Humidity and Temperature Sensor RHT03

nets:
  N1: Componente1.D11_PWM/MOSI, LCD1.E
  N2: Componente1.D12/MISO, LCD1.RS
  N3: Componente1.D2, LCD1.DB7
  N4: Componente1.D3_PWM, LCD1.DB6
  N5: Componente1.D4, LCD1.DB5
  N6: Componente1.D5_PWM, LCD1.DB4
  N7: Componente1.D7, RHT1.Data-signal
  5V: Componente1.5V, LCD1.VDD, LCD1.LED+, U1.E, RHT1.Vcc
  GND: Componente1.GND, LCD1.VSS, LCD1.R/W, LCD1.LED-, U1.A, RHT1.GND_2
  N8: LCD1.V0, U1.S

// code stored in the sketch: Untitled.ino

#include <LiquidCrystal.h> //Carrega a biblioteca LCD
#include <DHT.h> //Carrega a biblioteca DHT

//Define a ligação ao pino de dados do sensor
#define DHTPIN 7

//Define o tipo de sensor DHT utilizado
#define DHTTYPE DHT11

DHT dht(DHTPIN, DHTTYPE);

//Define os pinos que serão ligados ao LCD
LiquidCrystal lcd(12, 11, 5, 4, 3, 2);

//Array simbolo grau
byte grau[8] = { B00001100,
                 B00010010,
                 B00010010,
                 B00001100,
                 B00000000,
                 B00000000,
                 B00000000,
                 B00000000,
               };

void setup()
{
  Serial.begin(9600); //Inicializa a serial
  lcd.begin(16, 2); //Inicializa LCD
  lcd.clear(); //Limpa o LCD
  //Cria o caractere customizado com o simbolo do grau
  lcd.createChar(0, grau);
}

void loop()
{
  float h = dht.readHumidity(); //Le o valor da umidade
  float t = dht.readTemperature(); //Le o valor da temperatura
  lcd.setCursor(0, 0);
  lcd.print("Temp : ");
  lcd.print(" ");
  lcd.setCursor(7, 0);
  lcd.print(t, 1);
  lcd.setCursor(12, 0);

  //Mostra o simbolo do grau formado pelo array
  lcd.write((byte)0);

  //Mostra o simbolo do grau quadrado
  //lcd.print((char)223);

  lcd.setCursor(0, 1);
  lcd.print("Umid : ");
  lcd.print(" ");
  lcd.setCursor(7, 1);
  lcd.print(h, 1);
  lcd.setCursor(12, 1);
  lcd.print("%");

  //Intervalo recomendado para leitura do sensor
  delay(1000);
}
