# Fritzing sketch Genius (saved by Fritzing 0.9.2b)
breadboards: 1

parts:
  LED1 = LED - 5mm [color="Red (660nm)" package="5 mm [THT]"]
  LED2 = LED - 5mm [color="Yellow (595nm)" package="5 mm [THT]"]
  LED3 = LED - 5mm [color="Green (570nm)" package="5 mm [THT]"]
  LED4 = LED - 5mm [color="White (4500K)" package="5 mm [THT]"]
  S1 = Pushbutton [package="[THT]"]
  S2 = Pushbutton [package="[THT]"]
  S3 = Pushbutton [package="[THT]"]
  S4 = Pushbutton [package="[THT]"]
  R1 = Resistor [tolerance=±5% resistance=330 package=THT]
  R2 = Resistor [tolerance=±5% resistance=330 package=THT]
  R3 = Resistor [tolerance=±5% resistance=330 package=THT]
  R4 = Resistor [tolerance=±5% resistance=330 package=THT]
  R5 = Resistor [tolerance=±5% resistance=330 package=THT]
  R6 = Resistor [tolerance=±5% resistance=330 package=THT]
  R7 = Resistor [tolerance=±5% resistance=330 package=THT]
  R8 = Resistor [tolerance=±5% resistance=330 package=THT]
  Arduino1 = Arduino Uno (Rev3)

nets:
  N1: LED1.cathode, R1.Pin_0
  N2: LED1.anode, Arduino1.D7
  N3: LED2.cathode, R2.Pin_0
  N4: LED3.cathode, R3.Pin_0
  N5: LED4.cathode, R4.Pin_0
  N6: LED4.anode, Arduino1.D4
  N7: S1.Pin_1, S1.Pin_2, S2.Pin_1, S2.Pin_2, S3.Pin_1, S3.Pin_2, S4.Pin_1, S4.Pin_2, R1.Pin_1, R2.Pin_1, R3.Pin_1, R4.Pin_1, R5.Pin_1, R6.Pin_1, R7.Pin_1, R8.Pin_1, Arduino1.GND
  N8: S1.Pin_3, S1.Pin_4, R5.Pin_0
  N9: S2.Pin_3, S2.Pin_4, R6.Pin_0
  N10: S3.Pin_3, S3.Pin_4, R7.Pin_0
  N11: S4.Pin_3, S4.Pin_4, R8.Pin_0, Arduino1.D8
