# Fritzing sketch Controle de Leds (saved by Fritzing 0.9.2b)
breadboards: 1

parts:
  Componente1 = Arduino Mega 2560 (Rev3)
  LCD1 = LCD screen
  U1 = POT [package=pot_mammoth]
  LED2 = smd LED [color="Red (633nm)" package="0805 [SMD]"]
  LED3 = smd LED [color="Red (633nm)" package="0805 [SMD]"]
  LED4 = smd LED [color="Red (633nm)" package="0805 [SMD]"]
  LED5 = smd LED [color="Red (633nm)" package="0805 [SMD]"]
  LED6 = smd LED [color="Red (633nm)" package="0805 [SMD]"]
  R1 = Resistor [tolerance=±5% resistance=330 package=THT]
  R2 = Resistor [tolerance=±5% resistance=330 package=THT]
  R3 = Resistor [tolerance=±5% resistance=330 package=THT]
  R4 = Resistor [tolerance=±5% resistance=330 package=THT]
  R5 = Resistor [tolerance=±5% resistance=330 package=THT]

nets:
  N1: Componente1.A0, U1.A
  N2: Componente1.GND, LCD1.V0, LCD1.R/W, LCD1.LED-, U1.S, LED2.cathode, LED3.cathode, LED4.cathode, LED5.cathode, LED6.cathode
  N3: Componente1.D13_PWM, LCD1.RS
  N4: Componente1.D12_PWM, LCD1.E
  N5: Componente1.D11_PWM, LCD1.DB4
  N6: Componente1.D10_PWM, LCD1.DB5
  N7: Componente1.D9_PWM, LCD1.DB6
  N8: Componente1.D8_PWM, LCD1.DB7
  5V: Componente1.5V, LCD1.VDD, LCD1.LED+, U1.E
  N9: Componente1.D2_PWM, R1.Pin_0
  N10: Componente1.D3_PWM, R2.Pin_0
  N11: Componente1.D4_PWM, R3.Pin_0
  N12: Componente1.D5_PWM, R4.Pin_0
  N13: Componente1.D6_PWM, R5.Pin_0
  N14: LED2.anode, R1.Pin_1
  N15: LED3.anode, R2.Pin_1
  N16: LED4.anode, R3.Pin_1
  N17: LED5.anode, R4.Pin_1
  N18: LED6.anode, R5.Pin_1
